# Fritzing sketch tinyrace_gate (saved by Fritzing 0.9.10b)
breadboards: 1

parts:
  Bauteil1 = Arduino Nano (Rev3.0)
  IR_RECV_4 = smd LED [color="Red (633nm)" package="0603 [SMD]"]
  R_RECV_4 = Resistor [tolerance=±5% resistance=10k package="0402 [SMD]"]
  IR_RECV_3 = smd LED [color="Red (633nm)" package="0603 [SMD]"]
  R_RECV_3 = Resistor [tolerance=±5% resistance=10k package="0402 [SMD]"]
  R_RECV_2 = Resistor [tolerance=±5% resistance=10k package="0402 [SMD]"]
  R_RECV_1 = Resistor [tolerance=±5% resistance=10k package="0402 [SMD]"]
  IR_RECV_2 = smd LED [color="Red (633nm)" package="0603 [SMD]"]
  IR_RECV_1 = smd LED [color="Red (633nm)" package="0603 [SMD]"]
  IR_SEND_4 = smd LED [color="Red (633nm)" package="0603 [SMD]"]
  R_SEND_4 = Resistor [tolerance=±5% resistance=220 package="0603 [SMD]"]
  IR_SEND_3 = smd LED [color="Red (633nm)" package="0603 [SMD]"]
  IR_SEND_2 = smd LED [color="Red (633nm)" package="0603 [SMD]"]
  R_SEND_2 = Resistor [tolerance=±5% resistance=220 package="0603 [SMD]"]
  IR_SEND_1 = smd LED [color="Red (633nm)" package="0603 [SMD]"]
  R_SEND_1 = Resistor [tolerance=±5% resistance=220 package="0603 [SMD]"]
  R_SEND_3 = Resistor [tolerance=±5% resistance=220 package="0603 [SMD]"]
  S1 = Round Pushbutton
  R_S1 = Resistor [tolerance=±20% power=0.25 resistance=220 package=THT]
  S2 = Round Pushbutton
  R_S2 = Resistor [tolerance=±5% power=0.25 resistance=220 package=THT]
  S3 = Round Pushbutton
  R_S3 = Resistor [tolerance=±5% power=0.25 resistance=220 package=THT]
  S4 = Round Pushbutton
  R_S4 = Resistor [tolerance=±5% power=0.25 resistance=220 package=THT]
  neopixel_b = NeoPixel Stick [part_number=1426]
  neopixel_a = NeoPixel Stick [part_number=1426]
  LCD16x2 = LCD1602-I2C
  VCC1 = 4 x AAA Battery Mount

nets:
  GND: Bauteil1.GND, R_RECV_4.Pin_0, R_RECV_3.Pin_0, R_RECV_2.Pin_0, R_RECV_1.Pin_0, IR_SEND_4.cathode, IR_SEND_3.cathode, IR_SEND_2.cathode, IR_SEND_1.cathode, R_S1.Pin_1, R_S2.Pin_1, R_S3.Pin_1, R_S4.Pin_1, neopixel_b.GND, neopixel_a.GND, LCD16x2.GND, VCC1.-
  N1: Bauteil1.D2, S1.leg1, R_S1.Pin_0
  N2: Bauteil1.D3, S2.leg1, R_S2.Pin_0
  N3: Bauteil1.D4, S3.leg1, R_S3.Pin_0
  N4: Bauteil1.D5, S4.leg1, R_S4.Pin_0
  N5: Bauteil1.D6, neopixel_a.DATAIN
  N6: Bauteil1.A5, LCD16x2.SCL
  N7: Bauteil1.A4, LCD16x2.SDA
  N8: Bauteil1.A3, R_RECV_1.Pin_1, IR_RECV_1.anode
  N9: Bauteil1.A2, R_RECV_2.Pin_1, IR_RECV_2.anode
  N10: Bauteil1.A1, IR_RECV_3.anode, R_RECV_3.Pin_1
  N11: Bauteil1.A0, IR_RECV_4.anode, R_RECV_4.Pin_1
  5V: IR_RECV_4.cathode, IR_RECV_3.cathode, IR_RECV_2.cathode, IR_RECV_1.cathode, R_SEND_4.Pin_1, R_SEND_2.Pin_1, R_SEND_1.Pin_1, R_SEND_3.Pin_1, S1.leg0, S2.leg0, S3.leg0, S4.leg0, neopixel_b.+5V, neopixel_a.+5V, LCD16x2.VCC, VCC1.+
  N12: IR_SEND_4.anode, R_SEND_4.Pin_0
  N13: IR_SEND_3.anode, R_SEND_3.Pin_0
  N14: IR_SEND_2.anode, R_SEND_2.Pin_0
  N15: IR_SEND_1.anode, R_SEND_1.Pin_0
  N16: neopixel_b.DATAIN, neopixel_a.DATAOUT

custom parts:
  NeoPixel Stick: Make your own little LED strip arrangement with this stick of NeoPixel LEDs. We crammed 8 of the tiny 5050 (5mm x 5mm) smart RGB LEDs onto a PCB with mounting holes and a chainable design. Use only one microcontroller pin to control as many as you can chain together! Each LED is addressable as the driver chip is inside the LED. Each one has ~18mA constant current drive so the color will be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
  LCD1602-I2C: A standard character display, usually with 2x16 characters. Comes in many colors with LCM1602 IIC attached.
